// Logisim project 16-bit ALU.circ as structural Verilog: 15 circuits, main circuit Full Adder
module Half_adder (
  input  X,
  input  Y,
  output SUM,
  output CARRY
);

  and and_1 (CARRY, X, Y);
  xor xor_1 (SUM, X, Y);
endmodule

module Full_Adder (
  input  X,
  input  Y,
  input  CI,
  output SUM,
  output CARRY
);

  wire and_1_out, and_2_out, xor_1_out;

  xor xor_1 (xor_1_out, X, Y);
  and and_1 (and_1_out, X, Y);
  xor xor_2 (SUM, xor_1_out, CI);
  and and_2 (and_2_out, xor_1_out, CI);
  or or_1 (CARRY, and_2_out, and_1_out);
endmodule

module _16_bit_Adder (
  input  [15:0] B,
  input  [15:0] A,
  input  Select_Line,
  output Carry_OUT,
  output Overflow,
  output [15:0] SUM
);

  wire full_adder_1_sum, full_adder_2_carry, full_adder_2_sum, full_adder_3_carry, full_adder_3_sum,
       full_adder_4_carry, full_adder_4_sum, full_adder_5_carry, full_adder_5_sum, full_adder_6_carry,
       full_adder_6_sum, full_adder_7_carry, full_adder_7_sum, full_adder_8_carry, full_adder_8_sum,
       full_adder_9_carry, full_adder_9_sum, full_adder_10_carry, full_adder_10_sum, full_adder_11_carry,
       full_adder_11_sum, full_adder_12_carry, full_adder_12_sum, full_adder_13_carry, full_adder_13_sum,
       full_adder_14_carry, full_adder_14_sum, full_adder_15_carry, full_adder_15_sum, half_adder_1_carry,
       half_adder_1_sum;

  xor xor_1 (Overflow, Carry_OUT, full_adder_3_carry);
  Full_Adder full_adder_1 (.X(A[15]), .Y(B[15]), .CI(full_adder_3_carry), .SUM(full_adder_1_sum), .CARRY(Carry_OUT));
  and and_1 (SUM[15], full_adder_1_sum, Select_Line);
  Full_Adder full_adder_2 (
    .X(A[13]), .Y(B[13]), .CI(full_adder_4_carry), .SUM(full_adder_2_sum), .CARRY(full_adder_2_carry));
  Full_Adder full_adder_3 (
    .X(A[14]), .Y(B[14]), .CI(full_adder_2_carry), .SUM(full_adder_3_sum), .CARRY(full_adder_3_carry));
  and and_2 (SUM[14], full_adder_3_sum, Select_Line);
  and and_3 (SUM[13], full_adder_2_sum, Select_Line);
  Full_Adder full_adder_4 (
    .X(A[12]), .Y(B[12]), .CI(full_adder_5_carry), .SUM(full_adder_4_sum), .CARRY(full_adder_4_carry));
  Full_Adder full_adder_5 (
    .X(A[11]), .Y(B[11]), .CI(full_adder_7_carry), .SUM(full_adder_5_sum), .CARRY(full_adder_5_carry));
  and and_4 (SUM[11], full_adder_5_sum, Select_Line);
  and and_5 (SUM[12], full_adder_4_sum, Select_Line);
  Full_Adder full_adder_6 (
    .X(A[9]), .Y(B[9]), .CI(full_adder_9_carry), .SUM(full_adder_6_sum), .CARRY(full_adder_6_carry));
  Full_Adder full_adder_7 (
    .X(A[10]), .Y(B[10]), .CI(full_adder_6_carry), .SUM(full_adder_7_sum), .CARRY(full_adder_7_carry));
  and and_6 (SUM[9], full_adder_6_sum, Select_Line);
  and and_7 (SUM[10], full_adder_7_sum, Select_Line);
  Full_Adder full_adder_8 (
    .X(A[7]), .Y(B[7]), .CI(full_adder_11_carry), .SUM(full_adder_8_sum), .CARRY(full_adder_8_carry));
  Full_Adder full_adder_9 (
    .X(A[8]), .Y(B[8]), .CI(full_adder_8_carry), .SUM(full_adder_9_sum), .CARRY(full_adder_9_carry));
  and and_8 (SUM[8], full_adder_9_sum, Select_Line);
  and and_9 (SUM[7], full_adder_8_sum, Select_Line);
  Full_Adder full_adder_10 (
    .X(A[5]), .Y(B[5]), .CI(full_adder_12_carry), .SUM(full_adder_10_sum), .CARRY(full_adder_10_carry));
  Full_Adder full_adder_11 (
    .X(A[6]), .Y(B[6]), .CI(full_adder_10_carry), .SUM(full_adder_11_sum), .CARRY(full_adder_11_carry));
  and and_10 (SUM[6], full_adder_11_sum, Select_Line);
  and and_11 (SUM[5], full_adder_10_sum, Select_Line);
  Full_Adder full_adder_12 (
    .X(A[4]), .Y(B[4]), .CI(full_adder_13_carry), .SUM(full_adder_12_sum), .CARRY(full_adder_12_carry));
  Full_Adder full_adder_13 (
    .X(A[3]), .Y(B[3]), .CI(full_adder_15_carry), .SUM(full_adder_13_sum), .CARRY(full_adder_13_carry));
  and and_12 (SUM[4], full_adder_12_sum, Select_Line);
  and and_13 (SUM[3], full_adder_13_sum, Select_Line);
  Full_Adder full_adder_14 (
    .X(A[1]), .Y(B[1]), .CI(half_adder_1_carry), .SUM(full_adder_14_sum), .CARRY(full_adder_14_carry));
  Full_Adder full_adder_15 (
    .X(A[2]), .Y(B[2]), .CI(full_adder_14_carry), .SUM(full_adder_15_sum), .CARRY(full_adder_15_carry));
  and and_14 (SUM[1], full_adder_14_sum, Select_Line);
  and and_15 (SUM[2], full_adder_15_sum, Select_Line);
  Half_adder half_adder_1 (.X(A[0]), .Y(B[0]), .SUM(half_adder_1_sum), .CARRY(half_adder_1_carry));
  and and_16 (SUM[0], half_adder_1_sum, Select_Line);

  // Notes on the sheet:
  //   The first one from the right is half adder rest all are full adders
  //   Output = A+B
endmodule

module Half_subtractor (
  input  X,
  input  Y,
  output DIFF,
  output Bout
);

  wire not_1_out;

  not not_1 (not_1_out, X);
  xor xor_1 (DIFF, X, Y);
  and and_1 (Bout, not_1_out, Y);
endmodule

module Full_Subtractor (
  input  X,
  input  Y,
  input  BI,
  output DIFF,
  output BORROW_OUT
);

  wire and_1_out, and_2_out, not_1_out, not_2_out, xor_1_out;

  not not_1 (not_1_out, X);
  xor xor_1 (xor_1_out, X, Y);
  and and_1 (and_1_out, not_1_out, Y);
  not not_2 (not_2_out, xor_1_out);
  xor xor_2 (DIFF, xor_1_out, BI);
  and and_2 (and_2_out, not_2_out, BI);
  or or_1 (BORROW_OUT, and_2_out, and_1_out);
endmodule

module _16_bit_Subtractor (
  input  [15:0] B,
  input  [15:0] A,
  input  Select_Line,
  output Borrow_OUT,
  output Overflow,
  output [15:0] Difference
);

  wire full_subtractor_1_diff, full_subtractor_2_borrow_out, full_subtractor_2_diff,
       full_subtractor_3_borrow_out, full_subtractor_3_diff, full_subtractor_4_borrow_out,
       full_subtractor_4_diff, full_subtractor_5_borrow_out, full_subtractor_5_diff,
       full_subtractor_6_borrow_out, full_subtractor_6_diff, full_subtractor_7_borrow_out,
       full_subtractor_7_diff, full_subtractor_8_borrow_out, full_subtractor_8_diff,
       full_subtractor_9_borrow_out, full_subtractor_9_diff, full_subtractor_10_borrow_out,
       full_subtractor_10_diff, full_subtractor_11_borrow_out, full_subtractor_11_diff,
       full_subtractor_12_borrow_out, full_subtractor_12_diff, full_subtractor_13_borrow_out,
       full_subtractor_13_diff, full_subtractor_14_borrow_out, full_subtractor_14_diff,
       full_subtractor_15_borrow_out, full_subtractor_15_diff, half_subtractor_1_bout, half_subtractor_1_diff;

  xor xor_1 (Overflow, Borrow_OUT, full_subtractor_2_borrow_out);
  Full_Subtractor full_subtractor_1 (
    .X(A[15]), .Y(B[15]), .BI(full_subtractor_2_borrow_out), .DIFF(full_subtractor_1_diff),
    .BORROW_OUT(Borrow_OUT));
  and and_1 (Difference[15], full_subtractor_1_diff, Select_Line);
  Full_Subtractor full_subtractor_2 (
    .X(A[14]), .Y(B[14]), .BI(full_subtractor_3_borrow_out), .DIFF(full_subtractor_2_diff),
    .BORROW_OUT(full_subtractor_2_borrow_out));
  Full_Subtractor full_subtractor_3 (
    .X(A[13]), .Y(B[13]), .BI(full_subtractor_4_borrow_out), .DIFF(full_subtractor_3_diff),
    .BORROW_OUT(full_subtractor_3_borrow_out));
  and and_2 (Difference[13], full_subtractor_3_diff, Select_Line);
  and and_3 (Difference[14], full_subtractor_2_diff, Select_Line);
  Full_Subtractor full_subtractor_4 (
    .X(A[12]), .Y(B[12]), .BI(full_subtractor_5_borrow_out), .DIFF(full_subtractor_4_diff),
    .BORROW_OUT(full_subtractor_4_borrow_out));
  Full_Subtractor full_subtractor_5 (
    .X(A[11]), .Y(B[11]), .BI(full_subtractor_7_borrow_out), .DIFF(full_subtractor_5_diff),
    .BORROW_OUT(full_subtractor_5_borrow_out));
  and and_4 (Difference[12], full_subtractor_4_diff, Select_Line);
  and and_5 (Difference[11], full_subtractor_5_diff, Select_Line);
  Full_Subtractor full_subtractor_6 (
    .X(A[9]), .Y(B[9]), .BI(full_subtractor_9_borrow_out), .DIFF(full_subtractor_6_diff),
    .BORROW_OUT(full_subtractor_6_borrow_out));
  Full_Subtractor full_subtractor_7 (
    .X(A[10]), .Y(B[10]), .BI(full_subtractor_6_borrow_out), .DIFF(full_subtractor_7_diff),
    .BORROW_OUT(full_subtractor_7_borrow_out));
  and and_6 (Difference[10], full_subtractor_7_diff, Select_Line);
  and and_7 (Difference[9], full_subtractor_6_diff, Select_Line);
  Full_Subtractor full_subtractor_8 (
    .X(A[7]), .Y(B[7]), .BI(full_subtractor_10_borrow_out), .DIFF(full_subtractor_8_diff),
    .BORROW_OUT(full_subtractor_8_borrow_out));
  Full_Subtractor full_subtractor_9 (
    .X(A[8]), .Y(B[8]), .BI(full_subtractor_8_borrow_out), .DIFF(full_subtractor_9_diff),
    .BORROW_OUT(full_subtractor_9_borrow_out));
  and and_8 (Difference[8], full_subtractor_9_diff, Select_Line);
  and and_9 (Difference[7], full_subtractor_8_diff, Select_Line);
  Full_Subtractor full_subtractor_10 (
    .X(A[6]), .Y(B[6]), .BI(full_subtractor_11_borrow_out), .DIFF(full_subtractor_10_diff),
    .BORROW_OUT(full_subtractor_10_borrow_out));
  Full_Subtractor full_subtractor_11 (
    .X(A[5]), .Y(B[5]), .BI(full_subtractor_13_borrow_out), .DIFF(full_subtractor_11_diff),
    .BORROW_OUT(full_subtractor_11_borrow_out));
  and and_10 (Difference[6], full_subtractor_10_diff, Select_Line);
  and and_11 (Difference[5], full_subtractor_11_diff, Select_Line);
  Full_Subtractor full_subtractor_12 (
    .X(A[3]), .Y(B[3]), .BI(full_subtractor_14_borrow_out), .DIFF(full_subtractor_12_diff),
    .BORROW_OUT(full_subtractor_12_borrow_out));
  Full_Subtractor full_subtractor_13 (
    .X(A[4]), .Y(B[4]), .BI(full_subtractor_12_borrow_out), .DIFF(full_subtractor_13_diff),
    .BORROW_OUT(full_subtractor_13_borrow_out));
  and and_12 (Difference[3], full_subtractor_12_diff, Select_Line);
  and and_13 (Difference[4], full_subtractor_13_diff, Select_Line);
  Full_Subtractor full_subtractor_14 (
    .X(A[2]), .Y(B[2]), .BI(full_subtractor_15_borrow_out), .DIFF(full_subtractor_14_diff),
    .BORROW_OUT(full_subtractor_14_borrow_out));
  Full_Subtractor full_subtractor_15 (
    .X(A[1]), .Y(B[1]), .BI(half_subtractor_1_bout), .DIFF(full_subtractor_15_diff),
    .BORROW_OUT(full_subtractor_15_borrow_out));
  and and_14 (Difference[1], full_subtractor_15_diff, Select_Line);
  and and_15 (Difference[2], full_subtractor_14_diff, Select_Line);
  Half_subtractor half_subtractor_1 (.X(A[0]), .Y(B[0]), .DIFF(half_subtractor_1_diff), .Bout(half_subtractor_1_bout));
  and and_16 (Difference[0], half_subtractor_1_diff, Select_Line);

  // Notes on the sheet:
  //   The first one from the right is half subtractor rest all are full subtractors
  //   Output = A-B
endmodule

module Comparator (
  input  [15:0] B,
  input  [15:0] A,
  input  Select_Line,
  output A_B,
  output A_B_2,
  output A_B_3
);

  wire and_2_out, Bout, nor_1_out, not_1_out, or_1_out;
  wire [15:0] n16_bit_subtractor_1_difference;

  _16_bit_Subtractor u_16_bit_subtractor_1 (
    .B(B), .A(A), .Borrow_OUT(Bout), .Difference(n16_bit_subtractor_1_difference), .Select_Line(1'b1));  // open: Overflow
  and and_1 (A_B, Select_Line, and_2_out);
  and and_2 (and_2_out, Bout, or_1_out);
  or or_1 (or_1_out, n16_bit_subtractor_1_difference[15], n16_bit_subtractor_1_difference[14], n16_bit_subtractor_1_difference[13], n16_bit_subtractor_1_difference[12], n16_bit_subtractor_1_difference[11], n16_bit_subtractor_1_difference[10], n16_bit_subtractor_1_difference[9], n16_bit_subtractor_1_difference[8], n16_bit_subtractor_1_difference[7], n16_bit_subtractor_1_difference[6], n16_bit_subtractor_1_difference[5], n16_bit_subtractor_1_difference[4], n16_bit_subtractor_1_difference[3], n16_bit_subtractor_1_difference[2], n16_bit_subtractor_1_difference[1], n16_bit_subtractor_1_difference[0]);
  nor nor_1 (nor_1_out, and_2_out, not_1_out);
  and and_3 (A_B_2, Select_Line, nor_1_out);
  not not_1 (not_1_out, or_1_out);
  and and_4 (A_B_3, Select_Line, not_1_out);
endmodule

module AND (
  input  Select_Line,
  input  [15:0] A,
  input  [15:0] B,
  output [15:0] Output
);

  wire [15:0] and_1_out, bit_extender_1_out;

  assign bit_extender_1_out = {{15{Select_Line}}, Select_Line};  // Bit_Extender bit_extender_1
  assign and_1_out = A & B;  // AND_Gate and_1, 16 bits wide
  assign Output = bit_extender_1_out & and_1_out;  // AND_Gate and_2, 16 bits wide
endmodule

module OR (
  input  Select_Line,
  input  [15:0] A,
  input  [15:0] B,
  output [15:0] Output
);

  wire [15:0] bit_extender_1_out, or_1_out;

  assign bit_extender_1_out = {{15{Select_Line}}, Select_Line};  // Bit_Extender bit_extender_1
  assign or_1_out = A | B;  // OR_Gate or_1, 16 bits wide
  assign Output = bit_extender_1_out & or_1_out;  // AND_Gate and_1, 16 bits wide
endmodule

module Reset (
  input  [15:0] Input,
  input  Reset,
  output [15:0] Output
);

  wire not_1_out;

  not not_1 (not_1_out, Reset);
  and and_1 (Output[15], not_1_out, Input[15]);
  and and_2 (Output[13], not_1_out, Input[13]);
  and and_3 (Output[14], not_1_out, Input[14]);
  and and_4 (Output[12], not_1_out, Input[12]);
  and and_5 (Output[11], not_1_out, Input[11]);
  and and_6 (Output[10], not_1_out, Input[10]);
  and and_7 (Output[9], not_1_out, Input[9]);
  and and_8 (Output[8], not_1_out, Input[8]);
  and and_9 (Output[7], not_1_out, Input[7]);
  and and_10 (Output[6], not_1_out, Input[6]);
  and and_11 (Output[5], not_1_out, Input[5]);
  and and_12 (Output[4], not_1_out, Input[4]);
  and and_13 (Output[3], not_1_out, Input[3]);
  and and_14 (Output[1], not_1_out, Input[1]);
  and and_15 (Output[2], not_1_out, Input[2]);
  and and_16 (Output[0], not_1_out, Input[0]);
endmodule

module _4_1_mux (
  input  I3,
  input  I2,
  input  I1,
  input  I0,
  input  S0,
  input  S1,
  output Q
);

  wire and_1_out, and_2_out, and_3_out, and_4_out, not_1_out, not_2_out;

  not not_1 (not_1_out, S0);
  not not_2 (not_2_out, S1);
  and and_1 (and_1_out, I3, S0, S1);
  and and_2 (and_2_out, I2, not_1_out, S1);
  and and_3 (and_3_out, I1, S0, not_2_out);
  and and_4 (and_4_out, I0, not_1_out, not_2_out);
  or or_1 (Q, and_1_out, and_2_out, and_3_out, and_4_out);
endmodule

module Bidirectional_shift (
  input  Clear,
  input  CLK,
  input  S1,
  input  S0,
  input  Serial_Input_for_Shift_Right,
  input  Serial_input_for_shift_left,
  input  [15:0] Input,
  output [15:0] Output
);

  wire n4_1_mux_1_q, n4_1_mux_2_q, n4_1_mux_3_q, n4_1_mux_4_q, n4_1_mux_5_q, n4_1_mux_6_q, n4_1_mux_7_q,
       n4_1_mux_8_q, n4_1_mux_9_q, n4_1_mux_10_q, n4_1_mux_11_q, n4_1_mux_12_q, n4_1_mux_13_q, n4_1_mux_14_q,
       n4_1_mux_15_q, n4_1_mux_16_q;

  _4_1_mux u_4_1_mux_1 (
    .I3(Input[15]), .I2(Output[14]), .I1(Serial_Input_for_Shift_Right), .I0(Output[15]), .S0(S0), .S1(S1),
    .Q(n4_1_mux_1_q));
  D_Flip_Flop d_ff_1 (.clk(CLK), .D(n4_1_mux_1_q), .Q(Output[15]), .reset(Clear));  // open: Qn, preset, en
  _4_1_mux u_4_1_mux_2 (
    .I3(Input[14]), .I2(Output[13]), .I1(Output[15]), .I0(Output[14]), .S0(S0), .S1(S1), .Q(n4_1_mux_2_q));
  D_Flip_Flop d_ff_2 (.clk(CLK), .D(n4_1_mux_2_q), .Q(Output[14]), .reset(Clear));  // open: Qn, preset, en
  _4_1_mux u_4_1_mux_3 (
    .I3(Input[13]), .I2(Output[12]), .I1(Output[14]), .I0(Output[13]), .S0(S0), .S1(S1), .Q(n4_1_mux_3_q));
  D_Flip_Flop d_ff_3 (.clk(CLK), .D(n4_1_mux_3_q), .Q(Output[13]), .reset(Clear));  // open: Qn, preset, en
  D_Flip_Flop d_ff_4 (.clk(CLK), .D(n4_1_mux_4_q), .Q(Output[12]), .reset(Clear));  // open: Qn, preset, en
  _4_1_mux u_4_1_mux_4 (
    .I3(Input[12]), .I2(Output[11]), .I1(Output[13]), .I0(Output[12]), .S0(S0), .S1(S1), .Q(n4_1_mux_4_q));
  D_Flip_Flop d_ff_5 (.clk(CLK), .D(n4_1_mux_5_q), .Q(Output[11]), .reset(Clear));  // open: Qn, preset, en
  _4_1_mux u_4_1_mux_5 (
    .I3(Input[11]), .I2(Output[10]), .I1(Output[12]), .I0(Output[11]), .S0(S0), .S1(S1), .Q(n4_1_mux_5_q));
  D_Flip_Flop d_ff_6 (.clk(CLK), .D(n4_1_mux_6_q), .Q(Output[10]), .reset(Clear));  // open: Qn, preset, en
  D_Flip_Flop d_ff_7 (.clk(CLK), .D(n4_1_mux_7_q), .Q(Output[9]), .reset(Clear));  // open: Qn, preset, en
  _4_1_mux u_4_1_mux_6 (
    .I3(Input[10]), .I2(Output[9]), .I1(Output[11]), .I0(Output[10]), .S0(S0), .S1(S1), .Q(n4_1_mux_6_q));
  D_Flip_Flop d_ff_8 (.clk(CLK), .D(n4_1_mux_8_q), .Q(Output[8]), .reset(Clear));  // open: Qn, preset, en
  _4_1_mux u_4_1_mux_7 (
    .I3(Input[9]), .I2(Output[8]), .I1(Output[10]), .I0(Output[9]), .S0(S0), .S1(S1), .Q(n4_1_mux_7_q));
  D_Flip_Flop d_ff_9 (.clk(CLK), .D(n4_1_mux_9_q), .Q(Output[7]), .reset(Clear));  // open: Qn, preset, en
  _4_1_mux u_4_1_mux_8 (
    .I3(Input[8]), .I2(Output[7]), .I1(Output[9]), .I0(Output[8]), .S0(S0), .S1(S1), .Q(n4_1_mux_8_q));
  D_Flip_Flop d_ff_10 (.clk(CLK), .D(n4_1_mux_10_q), .Q(Output[6]), .reset(Clear));  // open: Qn, preset, en
  D_Flip_Flop d_ff_11 (.clk(CLK), .D(n4_1_mux_11_q), .Q(Output[5]), .reset(Clear));  // open: Qn, preset, en
  _4_1_mux u_4_1_mux_9 (
    .I3(Input[7]), .I2(Output[6]), .I1(Output[8]), .I0(Output[7]), .S0(S0), .S1(S1), .Q(n4_1_mux_9_q));
  D_Flip_Flop d_ff_12 (.clk(CLK), .D(n4_1_mux_12_q), .Q(Output[4]), .reset(Clear));  // open: Qn, preset, en
  _4_1_mux u_4_1_mux_10 (
    .I3(Input[6]), .I2(Output[5]), .I1(Output[7]), .I0(Output[6]), .S0(S0), .S1(S1), .Q(n4_1_mux_10_q));
  D_Flip_Flop d_ff_13 (.clk(CLK), .D(n4_1_mux_13_q), .Q(Output[3]), .reset(Clear));  // open: Qn, preset, en
  D_Flip_Flop d_ff_14 (.clk(CLK), .D(n4_1_mux_14_q), .Q(Output[2]), .reset(Clear));  // open: Qn, preset, en
  _4_1_mux u_4_1_mux_11 (
    .I3(Input[5]), .I2(Output[4]), .I1(Output[6]), .I0(Output[5]), .S0(S0), .S1(S1), .Q(n4_1_mux_11_q));
  D_Flip_Flop d_ff_15 (.clk(CLK), .D(n4_1_mux_15_q), .Q(Output[1]), .reset(Clear));  // open: Qn, preset, en
  _4_1_mux u_4_1_mux_12 (
    .I3(Input[4]), .I2(Output[3]), .I1(Output[5]), .I0(Output[4]), .S0(S0), .S1(S1), .Q(n4_1_mux_12_q));
  D_Flip_Flop d_ff_16 (.clk(CLK), .D(n4_1_mux_16_q), .Q(Output[0]), .reset(Clear));  // open: Qn, preset, en
  _4_1_mux u_4_1_mux_13 (
    .I3(Input[3]), .I2(Output[2]), .I1(Output[4]), .I0(Output[3]), .S0(S0), .S1(S1), .Q(n4_1_mux_13_q));
  _4_1_mux u_4_1_mux_14 (
    .I3(Input[2]), .I2(Output[1]), .I1(Output[3]), .I0(Output[2]), .S0(S0), .S1(S1), .Q(n4_1_mux_14_q));
  _4_1_mux u_4_1_mux_15 (
    .I3(Input[1]), .I2(Output[0]), .I1(Output[2]), .I0(Output[1]), .S0(S0), .S1(S1), .Q(n4_1_mux_15_q));
  _4_1_mux u_4_1_mux_16 (
    .I3(Input[0]), .I2(Serial_input_for_shift_left), .I1(Output[1]), .I0(Output[0]), .S0(S0), .S1(S1),
    .Q(n4_1_mux_16_q));
endmodule

module _3_8_Decoder (
  input  S0,
  input  S1,
  input  S2,
  output O0,
  output O1,
  output O2,
  output O3,
  output O4,
  output O5,
  output O6,
  output O7
);

  wire not_1_out, not_2_out, not_3_out;

  not not_1 (not_1_out, S0);
  not not_2 (not_2_out, S1);
  not not_3 (not_3_out, S2);
  and and_1 (O0, not_1_out, not_2_out, not_3_out);
  and and_2 (O1, not_1_out, not_2_out, S2);
  and and_3 (O2, not_1_out, S1, not_3_out);
  and and_4 (O3, not_1_out, S1, S2);
  and and_5 (O4, S0, not_2_out, not_3_out);
  and and_6 (O5, S0, not_2_out, S2);
  and and_7 (O6, S0, S1, not_3_out);
  and and_8 (O7, S0, S1, S2);
endmodule

module All_circuit_MUX (
  input  [15:0] A,
  input  [15:0] B,
  input  CLK,
  input  S0,
  input  S1,
  input  S2,
  input  Serial_Input_for_Shift_Right,
  input  Serial_Input_for_Shift_Left,
  input  Clear,
  output OverFlow_For_Adder,
  output OverFlow_For_Subtractor,
  output A_B,
  output A_B_2,
  output A_B_3,
  output [15:0] Output
);

  wire n3_8_decoder_1_o0, n3_8_decoder_1_o1, n3_8_decoder_1_o2, n3_8_decoder_1_o3, n3_8_decoder_1_o4,
       n3_8_decoder_1_o5, n3_8_decoder_1_o6, Reset;
  wire [15:0] and_1_output, bidirectional_shift_1_output, n16_bit_adder_1_sum,
       n16_bit_subtractor_1_difference, or_1_output, reset_1_output, reset_2_output;

  Reset reset_1 (.Input(A), .Reset(Reset), .Output(reset_1_output));
  Reset reset_2 (.Input(B), .Reset(Reset), .Output(reset_2_output));
  _3_8_Decoder u_3_8_decoder_1 (
    .S0(S0), .S1(S1), .S2(S2), .O0(n3_8_decoder_1_o0), .O1(n3_8_decoder_1_o1), .O2(n3_8_decoder_1_o2),
    .O3(n3_8_decoder_1_o3), .O4(n3_8_decoder_1_o4), .O5(n3_8_decoder_1_o5), .O6(n3_8_decoder_1_o6), .O7(Reset));
  Comparator comparator_1 (
    .B(reset_2_output), .A(reset_1_output), .A_B(A_B_3), .A_B_2(A_B_2), .A_B_3(A_B),
    .Select_Line(n3_8_decoder_1_o4));
  _16_bit_Adder u_16_bit_adder_1 (
    .B(reset_2_output), .A(reset_1_output), .SUM(n16_bit_adder_1_sum), .Overflow(OverFlow_For_Adder),
    .Select_Line(n3_8_decoder_1_o0));  // open: Carry_OUT
  _16_bit_Subtractor u_16_bit_subtractor_1 (
    .B(reset_2_output), .A(reset_1_output), .Difference(n16_bit_subtractor_1_difference),
    .Overflow(OverFlow_For_Subtractor), .Select_Line(n3_8_decoder_1_o1));  // open: Borrow_OUT
  AND and_1 (.Select_Line(n3_8_decoder_1_o2), .A(reset_1_output), .B(reset_2_output), .Output(and_1_output));
  OR or_1 (.Select_Line(n3_8_decoder_1_o3), .A(reset_1_output), .Output(or_1_output), .B(reset_2_output));
  Bidirectional_shift bidirectional_shift_1 (
    .Output(bidirectional_shift_1_output), .Serial_Input_for_Shift_Right(Serial_Input_for_Shift_Right),
    .S1(n3_8_decoder_1_o5), .S0(n3_8_decoder_1_o6),
    .Serial_input_for_shift_left(Serial_Input_for_Shift_Left), .Input(reset_1_output), .CLK(CLK),
    .Clear(Clear));
  assign Output = n16_bit_adder_1_sum | n16_bit_subtractor_1_difference | bidirectional_shift_1_output | and_1_output | or_1_output;  // OR_Gate or_2, 16 bits wide

  // Notes on the sheet:
  //   A: pull=down
  //   Adder
  //   Subtractor
  //   OR
  //   Comparator
  //   Shifter
endmodule

module _16_bit_ALU (
  input  [15:0] A,
  input  [15:0] B,
  input  S0,
  input  S1,
  input  S2,
  input  Serial_Input_for_Shift_Right,
  input  Serial_Input_for_Shift_Left,
  output Overflow_for_adder,
  output Overflow_for_subtractor,
  output A_B,
  output A_B_2,
  output A_B_3,
  output [15:0] Output
);

  wire Clear_out, CLK_out;

  Clock CLK (.out(CLK_out));
  Button Clear (.out(Clear_out));
  All_circuit_MUX all_circuit_mux_1 (
    .A(A), .B(B), .CLK(CLK_out), .S0(S0), .S1(S1), .S2(S2),
    .Serial_Input_for_Shift_Right(Serial_Input_for_Shift_Right),
    .Serial_Input_for_Shift_Left(Serial_Input_for_Shift_Left), .Clear(Clear_out),
    .OverFlow_For_Adder(Overflow_for_adder), .OverFlow_For_Subtractor(Overflow_for_subtractor), .A_B(A_B),
    .A_B_2(A_B_2), .A_B_3(A_B_3), .Output(Output));

  // Notes on the sheet:
  //   000 - Add
  //   001 - Subtract
  //   010 - AND
  //   011 - OR
  //   100 - Comparator
  //   101 - Shift Left
  //   110 - Shift Right
  //   111 - Rest
  //   A and B are Inputs, S0,S1 and S2 are Select Lines where MSB is S0 and LSB is S2
endmodule
